// Digital circuit I.dig as structural Verilog
module I (
  input  Mux1,
  input  [15:0] Ct,
  input  c0,
  output [23:0] Add
);

  wire [23:0] Contador_s, multiplexer_1_out;

  Add #(.Bits(24)) Contador (.a(Add), .b(24'h1), .c_i(1'b0), .s(Contador_s));  // open: c_o
  Multiplexer #(.Bits(24)) multiplexer_1 (
    .sel(Mux1), .in_0(Contador_s), .in_1({{8{1'b0}}, Ct}), .out(multiplexer_1_out));
  Register #(.Bits(24)) IP (.D(multiplexer_1_out), .C(c0), .en(c0), .Q(Add));

  // Other names for the same wires on the sheet: Ct_t[15:0] = Ct

  // Notes on the sheet:
  //   /* Ct em 16 bits, ampliado para 24 (quantia máx. de Bits aceita pela Rom.
  //   Só posso fazer condicionais com números abaixo de 16 bits */
  //   Entradas
endmodule
