// Digital circuit II.dig as structural Verilog
module II (
  input  Mux1,
  input  c0,
  output [3:0] Op,
  output [3:0] a,
  output [3:0] b,
  output [3:0] c,
  output [31:0] Ext
);

  wire [23:0] Apontador_add;

  I Apontador (.Mux1(Mux1), .Ct(Ext[15:0]), .c0(c0), .Add(Apontador_add));
  ROM #(.AddrBits(24), .Bits(32)) Programa_1 (.A(Apontador_add), .sel(1'b1), .D({Op, a, b, c, Ext[15:0]}));

  assign Ext[31:16] = {16{1'b0}};

  // Other names for the same wires on the sheet: Ct[15:0] = Ext[15:0]

  // Notes on the sheet:
  //   Entradas - I
  //   Ct
  //   C(1) := 4
  //   C(2) := 5
  //   C(3) := C(1) + C(2).
  //   contents of Programa_1 (hex, n*v repeats v):
  //   10004,20005,11230000,c3000000,21240000,c4000000,31250000,c5000000,41260000,c6000000,
  //   51270000,c7000000,61280000,c8000000,71090000,c9000000,810a00ff,ca000000,910b008f,
  //   cb000000,ffffffff
  //   0 — — 1 4
  //   0 — — 2 5
  //   1 1 2 3 —
  //   1*16bts
  //   4*4bts
endmodule
