// Digital circuit III.dig as structural Verilog
module III (
  input  c0,
  output [31:0] Display
);

  wire Mux1, Mux2, Mux3, Rwe, Smux1;
  wire [3:0] a, b, c, func, Op;
  wire [31:0] Ct, gama, multiplexer_1_out, Out, Vet_Reg_db;

  II Mem__de_Programa (.Mux1(Mux1), .c0(c0), .Op(Op), .a(a), .b(b), .c(c), .Ext(Ct));
  RegisterFile #(.AddrBits(4), .Bits(32)) Vet_Reg (
    .Din(gama), .we(Rwe), .Rw(c), .C(c0), .Ra(a), .Rb(b), .Da(Out), .Db(Vet_Reg_db));
  ROM #(.AddrBits(4), .Bits(8)) Mem__de_Control (.A(Op), .sel(1'b1), .D({Rwe, Smux1, Mux2, Mux3, func}));
  Verif_saida verif_saida_1 (.Op(Op), .Out(Out), .Display(Display));
  Multiplexer #(.Bits(32)) multiplexer_1 (.sel(Mux2), .in_0(Vet_Reg_db), .in_1(Ct), .out(multiplexer_1_out));
  ULA ula_1 (.alp(Out), .bet(multiplexer_1_out), .ULA(func), .g(gama));
  Verif_mux1 verif_mux1_1 (.Op(Op), .gama(gama), .Smux1(Smux1), .Mux1(Mux1));

  // Notes on the sheet:
  //   Entradas - I
  //   Mux-1
  //   Entradas - III
  //   Mux-2
  //   Verificador de Saída
  //   contents of Mem__de_Control (hex, n*v repeats v):
  //   a0,81,82,83,84,85,86,87,a5,a1,0,0,8f,cf,e
  //   Mux3? Que?
  //   Sinais de Controle
  //   Verificador de Mux1
endmodule
