// Digital circuit Mico-XI.dig as structural Verilog
module Mico_XI (
  input  Clock,
  output [31:0] Display
);

  III Mico_XI (.c0(Clock), .Display(Display));

  // Notes on the sheet:
  //   Clock: Hz: 3
endmodule
