// Digital circuit Multiplicador.dig as structural Verilog
module Multiplicador (
  input  [31:0] a,
  input  [31:0] b,
  output [31:0] _3
);

  wire [63:32] mul_1_mul;

  Mul #(.Bits(32)) mul_1 (.a(a), .b(b), .mul({mul_1_mul, _3}));
endmodule
