// Digital circuit Verif_mux1.dig as structural Verilog
module Verif_mux1 (
  input  [3:0] Op,
  input  [31:0] gama,
  input  Smux1,
  output Mux1
);

  wire a__eq__eq__b_eq, Estou_em_E_eq, multiplexer_1_out, multiplexer_2_out;

  comparador4 Estou_em_E (.a(Op), .b(4'b1110), .eq(Estou_em_E_eq));
  comparador32 a__eq__eq__b (.a(gama), .b({32{1'b1}}), .eq(a__eq__eq__b_eq));
  Multiplexer multiplexer_1 (.sel(Estou_em_E_eq), .in_0(1'b0), .in_1(a__eq__eq__b_eq), .out(multiplexer_1_out));
  Multiplexer multiplexer_2 (.sel(multiplexer_1_out), .in_0(1'b0), .in_1(1'b1), .out(multiplexer_2_out));
  or or_1 (Mux1, Smux1, multiplexer_2_out);

  // Notes on the sheet:
  //   Verificador de Mux1
endmodule
