// Digital circuit Verif_saida.dig as structural Verilog
module Verif_saida (
  input  [3:0] Op,
  input  [31:0] Out,
  output [31:0] Display
);

  wire comparador4_1_eq;

  comparador4 comparador4_1 (.a(Op), .b(4'b1100), .eq(comparador4_1_eq));
  Multiplexer #(.Bits(32)) multiplexer_1 (.sel(comparador4_1_eq), .in_0({32{1'b0}}), .in_1(Out), .out(Display));
endmodule
