// Digital circuit comparador32.dig as structural Verilog
module comparador32 (
  input  [31:0] a,
  input  [31:0] b,
  output eq
);

  wire x0, x1, x2, x3, x4, x5, x6, x7, x8, x9, x10, x11, x12, x13, x14, x15, x16, x17, x18, x19, x20, x21,
       x22, x23, x24, x25, x26, x27, x28, x29, x30, x31;

  assign {x31, x30, x29, x28, x27, x26, x25, x24, x23, x22, x21, x20, x19, x18, x17, x16, x15, x14, x13, x12, x11, x10, x9, x8, x7, x6, x5, x4, x3, x2, x1, x0} = ~(a ^ b);  // XNOr xnor_1, 32 bits wide
  and and_1 (eq, x0, x1, x2, x3, x4, x5, x6, x7, x8, x9, x10, x11, x12, x13, x14, x15, x16, x17, x18, x19, x20, x21, x22, x23, x24, x25, x26, x27, x28, x29, x30, x31);
endmodule
