// Digital circuit comparador4.dig as structural Verilog
module comparador4 (
  input  [3:0] a,
  input  [3:0] b,
  output eq
);

  wire x0, x1, x2, x3;

  assign {x3, x2, x1, x0} = ~(a ^ b);  // XNOr xnor_1, 4 bits wide
  and and_1 (eq, x0, x1, x2, x3);
endmodule
