// Digital circuit Programa1.dig as structural Verilog
module Programa1 (
  input  [23:0] in_1,
  output [31:0] out_2
);

  ROM #(.AddrBits(24), .Bits(32)) Programa_1 (.A(in_1), .sel(1'b1), .D(out_2));

  // Notes on the sheet:
  //   contents of Programa_1 (hex, n*v repeats v):
  //   10004,20005,11230000,c3000000,21240000,c4000000,31250000,c5000000,41260000,c6000000,
  //   51270000,c7000000,61280000,c8000000,71090000,c9000000,810a00ff,ca000000,910b008f,
  //   cb000000,ffffffff
endmodule
