// Digital circuit ULA.dig as structural Verilog
module ULA (
  input  [31:0] alp,
  input  [31:0] bet,
  input  [3:0] ULA,
  output [31:0] g
);

  wire comparador32_1_eq;
  wire [31:0] _1_9, _2, _3, _4, _5_8, _6, _7, _14;

  Add #(.Bits(32)) add_1 (.a(alp), .b(bet), .c_i(1'b0), .s(_1_9));  // open: c_o
  Sub #(.Bits(32)) sub_1 (.a(alp), .b(bet), .c_i(1'b0), .s(_2));  // open: c_o
  Multiplicador multiplicador_1 (.a(alp), .b(bet), ._3(_3));
  assign _4 = alp & bet;  // And and_1, 32 bits wide
  assign _5_8 = alp | bet;  // Or or_1, 32 bits wide
  assign _6 = alp ^ bet;  // XOr xor_1, 32 bits wide
  comparador32 comparador32_1 (.a(alp), .b(bet), .eq(comparador32_1_eq));
  assign _7 = ~alp;  // Not not_1, 32 bits wide
  Multiplexer #(.Bits(32)) multiplexer_1 (.sel(comparador32_1_eq), .in_0({32{1'b0}}), .in_1({32{1'b1}}), .out(_14));
  Multiplexer #(.Selector_Bits(4), .Bits(32)) multiplexer_2 (
    .sel(ULA), .in_0(bet), .in_1(_1_9), .in_2(_2), .in_3(_3), .in_4(_4), .in_5(_5_8), .in_6(_6), .in_7(_7),
    .in_8(_5_8), .in_9(_1_9), .in_10({32{1'b0}}), .in_11({32{1'b0}}), .in_12(alp), .in_13({32{1'b0}}),
    .in_14(_14), .in_15({32{1'b0}}), .out(g));

  // Other names for the same wires on the sheet: a[31:0] = alp; b[31:0] = bet

  // Notes on the sheet:
  //   ENTRADAS - ULA
  //   0 - envolve const.
  //   OPERAÇÕES
  //   12(c) - Display (ULA, aquiete-se por favor).
  //   8 - envolve const (Or)
  //   9 - envolve const (Soma)
  //   10(a) - Não implementar
  //   11(b) - Não implementar
  //   13(d) - Envolve IP (jump)
  //   14(e) - Compara igualdade
  //   15(f) - Envolve IP (xiu)
  //   SELEÇÃO
endmodule
